// Logisim project NAND2Tetris_logisim.circ as structural Verilog: 24 circuits, main circuit Computer
module Computer (
);

  wire cpu_1_writem, reset_out;
  wire [14:0] cpu_1_addressm, cpu_1_pc_out;
  wire [15:0] cpu_1_outm, memory_1_out16, rom_1_data;

  ROM #(.addrWidth(15), .dataWidth(16)) rom_1 (.addr(cpu_1_pc_out), .data(rom_1_data));
  Button reset (.out(reset_out));
  CPU cpu_1 (
    .writeM(cpu_1_writem), .instruction(rom_1_data), .outM(cpu_1_outm), .reset(reset_out),
    .PC_out(cpu_1_pc_out), .inM(memory_1_out16), .addressM(cpu_1_addressm));
  Memory memory_1 (.out16(memory_1_out16), .load(cpu_1_writem), .address15(cpu_1_addressm), .in16(cpu_1_outm));

  // Notes on the sheet:
  //   Hack Computer
endmodule

module Mux4Way16 (
  input  [15:0] a16,
  input  [15:0] b16,
  input  [15:0] c16,
  input  [15:0] d16,
  input  [1:0] sel2,
  output [15:0] out16
);

  wire [15:0] multiplexer_1_out, multiplexer_2_out;

  Multiplexer #(.width(16), .enable("false")) multiplexer_1 (
    .in0(a16), .in1(b16), .out(multiplexer_1_out), .sel(sel2[0]));
  Multiplexer #(.width(16), .enable("false")) multiplexer_2 (
    .in0(c16), .in1(d16), .out(multiplexer_2_out), .sel(sel2[0]));
  Multiplexer #(.width(16), .enable("false")) multiplexer_3 (
    .in0(multiplexer_1_out), .in1(multiplexer_2_out), .out(out16), .sel(sel2[1]));
endmodule

module Mux8Way16 (
  input  [15:0] a16,
  input  [15:0] b16,
  input  [15:0] c16,
  input  [15:0] d16,
  input  [15:0] e16,
  input  [15:0] f16,
  input  [15:0] g16,
  input  [15:0] h16,
  input  [2:0] sel3,
  output [15:0] out16
);

  wire [15:0] mux4way16_1_out16, mux4way16_2_out16;

  Mux4Way16 mux4way16_1 (.a16(a16), .b16(b16), .c16(c16), .d16(d16), .sel2(sel3[1:0]), .out16(mux4way16_1_out16));
  Mux4Way16 mux4way16_2 (.a16(e16), .b16(f16), .c16(g16), .d16(h16), .sel2(sel3[1:0]), .out16(mux4way16_2_out16));
  Multiplexer #(.width(16), .enable("false")) multiplexer_1 (
    .in0(mux4way16_1_out16), .in1(mux4way16_2_out16), .out(out16), .sel(sel3[2]));
endmodule

module Or8Way (
  input  [7:0] in8,
  output out1
);

  wire or_1_out, or_2_out, or_3_out, or_4_out, or_5_out, or_6_out;

  or or_1 (or_1_out, in8[0], in8[1]);
  or or_2 (or_2_out, in8[2], in8[3]);
  or or_3 (or_3_out, in8[4], in8[5]);
  or or_4 (or_4_out, in8[6], in8[7]);
  or or_5 (or_5_out, or_1_out, or_2_out);
  or or_6 (or_6_out, or_3_out, or_4_out);
  or or_7 (out1, or_5_out, or_6_out);
endmodule

module DMux4Way (
  input  in1,
  input  [1:0] sel2,
  output a1,
  output b1,
  output c1,
  output d1
);

  wire demultiplexer_1_out0, demultiplexer_1_out1;

  Demultiplexer #(.enable("false")) demultiplexer_1 (
    .out0(demultiplexer_1_out0), .out1(demultiplexer_1_out1), .in(in1), .sel(sel2[1]));
  Demultiplexer #(.enable("false")) demultiplexer_2 (.out0(a1), .out1(b1), .in(demultiplexer_1_out0), .sel(sel2[0]));
  Demultiplexer #(.enable("false")) demultiplexer_3 (.out0(c1), .out1(d1), .in(demultiplexer_1_out1), .sel(sel2[0]));
endmodule

module DMux8Way (
  input  in1,
  input  [2:0] sel3,
  output a1,
  output b1,
  output c1,
  output d1,
  output e1,
  output f1,
  output g1,
  output h1
);

  wire demultiplexer_1_out0, demultiplexer_1_out1;

  Demultiplexer #(.enable("false")) demultiplexer_1 (
    .out0(demultiplexer_1_out0), .out1(demultiplexer_1_out1), .in(in1), .sel(sel3[2]));
  DMux4Way dmux4way_1 (.in1(demultiplexer_1_out0), .sel2(sel3[1:0]), .a1(a1), .b1(b1), .c1(c1), .d1(d1));
  DMux4Way dmux4way_2 (.in1(demultiplexer_1_out1), .sel2(sel3[1:0]), .a1(e1), .b1(f1), .c1(g1), .d1(h1));
endmodule

module HalfAdder (
  input  a,
  input  b,
  output sum,
  output carry
);

  xor xor_1 (sum, a, b);
  and and_1 (carry, a, b);
endmodule

module FullAdder (
  input  a,
  input  b,
  input  c,
  output sum,
  output carry
);

  wire halfadder_1_carry, halfadder_1_sum, halfadder_2_carry;

  HalfAdder halfadder_1 (.a(a), .b(b), .sum(halfadder_1_sum), .carry(halfadder_1_carry));
  HalfAdder halfadder_2 (.a(halfadder_1_sum), .b(c), .sum(sum), .carry(halfadder_2_carry));
  xor xor_1 (carry, halfadder_2_carry, halfadder_1_carry);
endmodule

module Add16 (
  input  [15:0] a16,
  input  [15:0] b16,
  output [15:0] out16
);

  wire fulladder_1_carry, fulladder_2_carry, fulladder_3_carry, fulladder_4_carry, fulladder_5_carry,
       fulladder_6_carry, fulladder_7_carry, fulladder_8_carry, fulladder_9_carry, fulladder_10_carry,
       fulladder_11_carry, fulladder_12_carry, fulladder_13_carry, fulladder_14_carry, fulladder_15_carry,
       halfadder_1_carry;

  HalfAdder halfadder_1 (.a(a16[0]), .b(b16[0]), .sum(out16[0]), .carry(halfadder_1_carry));
  FullAdder fulladder_1 (.carry(fulladder_1_carry), .sum(out16[1]), .b(b16[1]), .a(a16[1]), .c(halfadder_1_carry));
  FullAdder fulladder_2 (.carry(fulladder_2_carry), .sum(out16[2]), .b(b16[2]), .a(a16[2]), .c(fulladder_1_carry));
  FullAdder fulladder_3 (.carry(fulladder_3_carry), .sum(out16[3]), .b(b16[3]), .a(a16[3]), .c(fulladder_2_carry));
  FullAdder fulladder_4 (.carry(fulladder_4_carry), .sum(out16[4]), .b(b16[4]), .a(a16[4]), .c(fulladder_3_carry));
  FullAdder fulladder_5 (.carry(fulladder_5_carry), .sum(out16[5]), .b(b16[5]), .a(a16[5]), .c(fulladder_4_carry));
  FullAdder fulladder_6 (.carry(fulladder_6_carry), .sum(out16[6]), .b(b16[6]), .a(a16[6]), .c(fulladder_5_carry));
  FullAdder fulladder_7 (.carry(fulladder_7_carry), .sum(out16[7]), .b(b16[7]), .a(a16[7]), .c(fulladder_6_carry));
  FullAdder fulladder_8 (.carry(fulladder_8_carry), .sum(out16[8]), .b(b16[8]), .a(a16[8]), .c(fulladder_7_carry));
  FullAdder fulladder_9 (.carry(fulladder_9_carry), .sum(out16[9]), .b(b16[9]), .a(a16[9]), .c(fulladder_8_carry));
  FullAdder fulladder_10 (.carry(fulladder_10_carry), .sum(out16[10]), .b(b16[10]), .a(a16[10]), .c(fulladder_9_carry));
  FullAdder fulladder_11 (
    .carry(fulladder_11_carry), .sum(out16[11]), .b(b16[11]), .a(a16[11]), .c(fulladder_10_carry));
  FullAdder fulladder_12 (
    .carry(fulladder_12_carry), .sum(out16[12]), .b(b16[12]), .a(a16[12]), .c(fulladder_11_carry));
  FullAdder fulladder_13 (
    .carry(fulladder_13_carry), .sum(out16[13]), .b(b16[13]), .a(a16[13]), .c(fulladder_12_carry));
  FullAdder fulladder_14 (
    .carry(fulladder_14_carry), .sum(out16[14]), .b(b16[14]), .a(a16[14]), .c(fulladder_13_carry));
  FullAdder fulladder_15 (
    .carry(fulladder_15_carry), .sum(out16[15]), .b(b16[15]), .a(a16[15]), .c(fulladder_14_carry));
  LED led_1 (.in(fulladder_15_carry));
endmodule

module Inc16 (
  input  [15:0] in16,
  output [15:0] out16
);

  wire halfadder_1_carry, halfadder_2_carry, halfadder_3_carry, halfadder_4_carry, halfadder_5_carry,
       halfadder_6_carry, halfadder_7_carry, halfadder_8_carry, halfadder_9_carry, halfadder_10_carry,
       halfadder_11_carry, halfadder_12_carry, halfadder_13_carry, halfadder_14_carry, halfadder_15_carry;

  HalfAdder halfadder_1 (.a(in16[0]), .b(1'b1), .sum(out16[0]), .carry(halfadder_1_carry));
  HalfAdder halfadder_2 (.a(in16[1]), .b(halfadder_1_carry), .sum(out16[1]), .carry(halfadder_2_carry));
  HalfAdder halfadder_3 (.a(in16[2]), .b(halfadder_2_carry), .sum(out16[2]), .carry(halfadder_3_carry));
  HalfAdder halfadder_4 (.a(in16[3]), .b(halfadder_3_carry), .sum(out16[3]), .carry(halfadder_4_carry));
  HalfAdder halfadder_5 (.a(in16[4]), .b(halfadder_4_carry), .sum(out16[4]), .carry(halfadder_5_carry));
  HalfAdder halfadder_6 (.a(in16[5]), .b(halfadder_5_carry), .sum(out16[5]), .carry(halfadder_6_carry));
  HalfAdder halfadder_7 (.a(in16[6]), .b(halfadder_6_carry), .sum(out16[6]), .carry(halfadder_7_carry));
  HalfAdder halfadder_8 (.a(in16[7]), .b(halfadder_7_carry), .sum(out16[7]), .carry(halfadder_8_carry));
  HalfAdder halfadder_9 (.a(in16[8]), .b(halfadder_8_carry), .sum(out16[8]), .carry(halfadder_9_carry));
  HalfAdder halfadder_10 (.a(in16[9]), .b(halfadder_9_carry), .sum(out16[9]), .carry(halfadder_10_carry));
  HalfAdder halfadder_11 (.a(in16[10]), .b(halfadder_10_carry), .sum(out16[10]), .carry(halfadder_11_carry));
  HalfAdder halfadder_12 (.a(in16[11]), .b(halfadder_11_carry), .sum(out16[11]), .carry(halfadder_12_carry));
  HalfAdder halfadder_13 (.a(in16[12]), .b(halfadder_12_carry), .sum(out16[12]), .carry(halfadder_13_carry));
  HalfAdder halfadder_14 (.a(in16[13]), .b(halfadder_13_carry), .sum(out16[13]), .carry(halfadder_14_carry));
  HalfAdder halfadder_15 (.a(in16[14]), .b(halfadder_14_carry), .sum(out16[14]), .carry(halfadder_15_carry));
  HalfAdder halfadder_16 (.a(in16[15]), .b(halfadder_15_carry), .sum(out16[15]));  // open: carry
endmodule

module ALU (
  input  [15:0] x,
  input  zx,
  input  nx,
  input  [15:0] y,
  input  zy,
  input  ny,
  input  f,
  input  no,
  output zr,
  output [15:0] out16,
  output ng
);

  wire or16way_1_out1;
  wire [15:0] add16_1_out16, and_1_out, and_2_out, and_3_out, multiplexer_1_out, multiplexer_2_out,
       multiplexer_3_out, multiplexer_4_out, multiplexer_5_out, not_1_out, not_2_out, not_3_out, not_4_out,
       not_5_out;

  assign not_1_out = ~x;  // NOT_Gate not_1, 16 bits wide
  assign not_2_out = ~y;  // NOT_Gate not_2, 16 bits wide
  Multiplexer #(.width(16), .enable("false")) multiplexer_1 (
    .in0(x), .in1(and_1_out), .out(multiplexer_1_out), .sel(zx));
  assign and_1_out = not_1_out & x;  // AND_Gate and_1, 16 bits wide
  Multiplexer #(.width(16), .enable("false")) multiplexer_2 (
    .in0(y), .in1(and_2_out), .out(multiplexer_2_out), .sel(zy));
  assign and_2_out = not_2_out & y;  // AND_Gate and_2, 16 bits wide
  Multiplexer #(.width(16), .enable("false")) multiplexer_3 (
    .in0(multiplexer_1_out), .in1(not_3_out), .out(multiplexer_3_out), .sel(nx));
  assign not_3_out = ~multiplexer_1_out;  // NOT_Gate not_3, 16 bits wide
  Multiplexer #(.width(16), .enable("false")) multiplexer_4 (
    .in0(multiplexer_2_out), .in1(not_4_out), .out(multiplexer_4_out), .sel(ny));
  assign not_4_out = ~multiplexer_2_out;  // NOT_Gate not_4, 16 bits wide
  assign and_3_out = multiplexer_3_out & multiplexer_4_out;  // AND_Gate and_3, 16 bits wide
  Add16 add16_1 (.a16(multiplexer_3_out), .b16(multiplexer_4_out), .out16(add16_1_out16));
  Multiplexer #(.width(16), .enable("false")) multiplexer_5 (
    .in0(and_3_out), .in1(add16_1_out16), .out(multiplexer_5_out), .sel(f));
  Multiplexer #(.width(16), .enable("false")) multiplexer_6 (
    .in0(multiplexer_5_out), .in1(not_5_out), .out({ng, out16[14:0]}), .sel(no));
  assign not_5_out = ~multiplexer_5_out;  // NOT_Gate not_5, 16 bits wide
  Or16Way or16way_1 (.in16({ng, out16[14:0]}), .out1(or16way_1_out1));
  not not_6 (zr, or16way_1_out1);

  assign out16[15] = ng;
endmodule

module Or16Way (
  input  [15:0] in16,
  output out1
);

  wire or8way_1_out1, or8way_2_out1;

  Or8Way or8way_1 (.in8(in16[7:0]), .out1(or8way_1_out1));
  Or8Way or8way_2 (.in8(in16[15:8]), .out1(or8way_2_out1));
  or or_1 (out1, or8way_1_out1, or8way_2_out1);
endmodule

module Bit (
  input  in1,
  input  load,
  input  in_3,
  output out1
);

  wire multiplexer_1_out;

  Multiplexer #(.enable("false")) multiplexer_1 (.in0(out1), .in1(in1), .out(multiplexer_1_out), .sel(load));
  D_Flip_Flop d_ff_1 (.D(multiplexer_1_out), .clk(in_3), .Q(out1));  // open: Qn, preset, reset
endmodule

module Register16 (
  input  [15:0] in16,
  input  clk,
  input  load,
  output [15:0] out16
);

  Bit bit_1 (.in1(in16[0]), .load(load), .in_3(clk), .out1(out16[0]));
  Bit bit_2 (.in1(in16[1]), .load(load), .in_3(clk), .out1(out16[1]));
  Bit bit_3 (.in1(in16[2]), .load(load), .in_3(clk), .out1(out16[2]));
  Bit bit_4 (.in1(in16[3]), .load(load), .in_3(clk), .out1(out16[3]));
  Bit bit_5 (.in1(in16[4]), .load(load), .in_3(clk), .out1(out16[4]));
  Bit bit_6 (.in1(in16[5]), .load(load), .in_3(clk), .out1(out16[5]));
  Bit bit_7 (.in1(in16[6]), .load(load), .in_3(clk), .out1(out16[6]));
  Bit bit_8 (.in1(in16[7]), .load(load), .in_3(clk), .out1(out16[7]));
  Bit bit_9 (.in1(in16[8]), .load(load), .in_3(clk), .out1(out16[8]));
  Bit bit_10 (.in1(in16[9]), .load(load), .in_3(clk), .out1(out16[9]));
  Bit bit_11 (.in1(in16[10]), .load(load), .in_3(clk), .out1(out16[10]));
  Bit bit_12 (.in1(in16[11]), .load(load), .in_3(clk), .out1(out16[11]));
  Bit bit_13 (.in1(in16[12]), .load(load), .in_3(clk), .out1(out16[12]));
  Bit bit_14 (.in1(in16[13]), .load(load), .in_3(clk), .out1(out16[13]));
  Bit bit_15 (.in1(in16[14]), .load(load), .in_3(clk), .out1(out16[14]));
  Bit bit_16 (.in1(in16[15]), .load(load), .in_3(clk), .out1(out16[15]));
endmodule

module RAM8 (
  input  load,
  input  [2:0] address,
  input  [15:0] in16,
  output [15:0] out16
);

  wire clock_1_out, demultiplexer_1_out0, demultiplexer_1_out1, demultiplexer_1_out2, demultiplexer_1_out3,
       demultiplexer_1_out4, demultiplexer_1_out5, demultiplexer_1_out6, demultiplexer_1_out7;
  wire [15:0] register_1_q, register_2_q, register_3_q, register_4_q, register_5_q, register_6_q,
       register_7_q, register_8_q;

  Demultiplexer #(.select(3), .enable("false")) demultiplexer_1 (
    .out0(demultiplexer_1_out0), .out1(demultiplexer_1_out1), .out2(demultiplexer_1_out2),
    .out3(demultiplexer_1_out3), .out4(demultiplexer_1_out4), .out5(demultiplexer_1_out5),
    .out6(demultiplexer_1_out6), .out7(demultiplexer_1_out7), .in(load), .sel(address));
  Clock clock_1 (.out(clock_1_out));
  Register #(.width(16)) register_1 (
    .D(in16), .en(demultiplexer_1_out0), .clk(clock_1_out), .Q(register_1_q));  // open: clr
  Register #(.width(16)) register_2 (
    .D(in16), .en(demultiplexer_1_out1), .clk(clock_1_out), .Q(register_2_q));  // open: clr
  Register #(.width(16)) register_3 (
    .D(in16), .en(demultiplexer_1_out2), .clk(clock_1_out), .Q(register_3_q));  // open: clr
  Register #(.width(16)) register_4 (
    .D(in16), .en(demultiplexer_1_out3), .clk(clock_1_out), .Q(register_4_q));  // open: clr
  Register #(.width(16)) register_5 (
    .D(in16), .en(demultiplexer_1_out4), .clk(clock_1_out), .Q(register_5_q));  // open: clr
  Register #(.width(16)) register_6 (
    .D(in16), .en(demultiplexer_1_out5), .clk(clock_1_out), .Q(register_6_q));  // open: clr
  Register #(.width(16)) register_7 (
    .D(in16), .en(demultiplexer_1_out6), .clk(clock_1_out), .Q(register_7_q));  // open: clr
  Register #(.width(16)) register_8 (
    .D(in16), .en(demultiplexer_1_out7), .clk(clock_1_out), .Q(register_8_q));  // open: clr
  Multiplexer #(.select(3), .width(16), .enable("false")) multiplexer_1 (
    .in0(register_1_q), .in1(register_2_q), .in2(register_3_q), .in3(register_4_q), .in4(register_5_q),
    .in5(register_6_q), .in6(register_7_q), .in7(register_8_q), .out(out16), .sel(address));
endmodule

module RAM64 (
  input  [15:0] in16,
  input  [5:0] address,
  input  load,
  output [15:0] out16
);

  wire demultiplexer_1_out0, demultiplexer_1_out1, demultiplexer_1_out2, demultiplexer_1_out3,
       demultiplexer_1_out4, demultiplexer_1_out5, demultiplexer_1_out6, demultiplexer_1_out7;
  wire [15:0] ram8_1_out16, ram8_2_out16, ram8_3_out16, ram8_4_out16, ram8_5_out16, ram8_6_out16,
       ram8_7_out16, ram8_8_out16;

  Demultiplexer #(.select(3), .enable("false")) demultiplexer_1 (
    .out0(demultiplexer_1_out0), .out1(demultiplexer_1_out1), .out2(demultiplexer_1_out2),
    .out3(demultiplexer_1_out3), .out4(demultiplexer_1_out4), .out5(demultiplexer_1_out5),
    .out6(demultiplexer_1_out6), .out7(demultiplexer_1_out7), .in(load), .sel(address[2:0]));
  RAM8 ram8_1 (.load(demultiplexer_1_out0), .address(address[5:3]), .out16(ram8_1_out16), .in16(in16));
  RAM8 ram8_2 (.load(demultiplexer_1_out1), .address(address[5:3]), .out16(ram8_2_out16), .in16(in16));
  RAM8 ram8_3 (.load(demultiplexer_1_out2), .address(address[5:3]), .out16(ram8_3_out16), .in16(in16));
  RAM8 ram8_4 (.load(demultiplexer_1_out3), .address(address[5:3]), .out16(ram8_4_out16), .in16(in16));
  RAM8 ram8_5 (.load(demultiplexer_1_out4), .address(address[5:3]), .out16(ram8_5_out16), .in16(in16));
  RAM8 ram8_6 (.load(demultiplexer_1_out5), .address(address[5:3]), .out16(ram8_6_out16), .in16(in16));
  RAM8 ram8_7 (.load(demultiplexer_1_out6), .address(address[5:3]), .out16(ram8_7_out16), .in16(in16));
  RAM8 ram8_8 (.load(demultiplexer_1_out7), .address(address[5:3]), .out16(ram8_8_out16), .in16(in16));
  Multiplexer #(.select(3), .width(16), .enable("false")) multiplexer_1 (
    .in0(ram8_1_out16), .in1(ram8_2_out16), .in2(ram8_3_out16), .in3(ram8_4_out16), .in4(ram8_5_out16),
    .in5(ram8_6_out16), .in6(ram8_7_out16), .in7(ram8_8_out16), .out(out16), .sel(address[2:0]));
endmodule

module RAM512 (
  input  [15:0] in16,
  input  load,
  input  [8:0] address,
  output [15:0] out16
);

  wire demultiplexer_1_out0, demultiplexer_1_out1, demultiplexer_1_out2, demultiplexer_1_out3,
       demultiplexer_1_out4, demultiplexer_1_out5, demultiplexer_1_out6, demultiplexer_1_out7;
  wire [15:0] ram64_1_out16, ram64_2_out16, ram64_3_out16, ram64_4_out16, ram64_5_out16, ram64_6_out16,
       ram64_7_out16, ram64_8_out16;

  Demultiplexer #(.select(3), .enable("false")) demultiplexer_1 (
    .out0(demultiplexer_1_out0), .out1(demultiplexer_1_out1), .out2(demultiplexer_1_out2),
    .out3(demultiplexer_1_out3), .out4(demultiplexer_1_out4), .out5(demultiplexer_1_out5),
    .out6(demultiplexer_1_out6), .out7(demultiplexer_1_out7), .in(load), .sel(address[2:0]));
  RAM64 ram64_1 (.in16(in16), .address(address[8:3]), .load(demultiplexer_1_out0), .out16(ram64_1_out16));
  RAM64 ram64_2 (.in16(in16), .address(address[8:3]), .load(demultiplexer_1_out1), .out16(ram64_2_out16));
  RAM64 ram64_3 (.in16(in16), .address(address[8:3]), .load(demultiplexer_1_out2), .out16(ram64_3_out16));
  RAM64 ram64_4 (.in16(in16), .address(address[8:3]), .load(demultiplexer_1_out3), .out16(ram64_4_out16));
  RAM64 ram64_5 (.in16(in16), .address(address[8:3]), .load(demultiplexer_1_out4), .out16(ram64_5_out16));
  RAM64 ram64_6 (.in16(in16), .address(address[8:3]), .load(demultiplexer_1_out5), .out16(ram64_6_out16));
  RAM64 ram64_7 (.in16(in16), .address(address[8:3]), .load(demultiplexer_1_out6), .out16(ram64_7_out16));
  RAM64 ram64_8 (.in16(in16), .address(address[8:3]), .load(demultiplexer_1_out7), .out16(ram64_8_out16));
  Multiplexer #(.select(3), .width(16), .enable("false")) multiplexer_1 (
    .in0(ram64_1_out16), .in1(ram64_2_out16), .in2(ram64_3_out16), .in3(ram64_4_out16), .in4(ram64_5_out16),
    .in5(ram64_6_out16), .in6(ram64_7_out16), .in7(ram64_8_out16), .out(out16), .sel(address[2:0]));

  // Notes on the sheet:
  //   RAM512
endmodule

module RAM8_34811e39 (
  input  load,
  input  [2:0] address,
  input  [15:0] in16,
  output [15:0] out16
);

  wire clock_1_out, dmux8way_1_a1, dmux8way_1_b1, dmux8way_1_c1, dmux8way_1_d1, dmux8way_1_e1, dmux8way_1_f1,
       dmux8way_1_g1, dmux8way_1_h1;
  wire [15:0] register16_1_out16, register16_2_out16, register16_3_out16, register16_4_out16,
       register16_5_out16, register16_6_out16, register16_7_out16, register16_8_out16;

  DMux8Way dmux8way_1 (
    .in1(load), .sel3(address), .a1(dmux8way_1_a1), .b1(dmux8way_1_b1), .c1(dmux8way_1_c1),
    .d1(dmux8way_1_d1), .e1(dmux8way_1_e1), .f1(dmux8way_1_f1), .g1(dmux8way_1_g1), .h1(dmux8way_1_h1));
  Clock clock_1 (.out(clock_1_out));
  Register16 register16_1 (.in16(in16), .clk(clock_1_out), .load(dmux8way_1_a1), .out16(register16_1_out16));
  Register16 register16_2 (.in16(in16), .clk(clock_1_out), .load(dmux8way_1_b1), .out16(register16_2_out16));
  Register16 register16_3 (.in16(in16), .clk(clock_1_out), .load(dmux8way_1_c1), .out16(register16_3_out16));
  Register16 register16_4 (.in16(in16), .clk(clock_1_out), .load(dmux8way_1_d1), .out16(register16_4_out16));
  Register16 register16_5 (.in16(in16), .clk(clock_1_out), .load(dmux8way_1_e1), .out16(register16_5_out16));
  Register16 register16_6 (.in16(in16), .clk(clock_1_out), .load(dmux8way_1_f1), .out16(register16_6_out16));
  Register16 register16_7 (.in16(in16), .clk(clock_1_out), .load(dmux8way_1_g1), .out16(register16_7_out16));
  Register16 register16_8 (.in16(in16), .clk(clock_1_out), .load(dmux8way_1_h1), .out16(register16_8_out16));
  Mux8Way16 mux8way16_1 (
    .a16(register16_1_out16), .b16(register16_2_out16), .c16(register16_3_out16), .d16(register16_4_out16),
    .e16(register16_5_out16), .f16(register16_6_out16), .g16(register16_7_out16), .h16(register16_8_out16),
    .sel3(address), .out16(out16));

  // Notes on the sheet:
  //   RAM8
endmodule

module RAM4K (
  input  [15:0] in16,
  input  load,
  input  [11:0] address,
  output [15:0] out16
);

  wire demultiplexer_1_out0, demultiplexer_1_out1, demultiplexer_1_out2, demultiplexer_1_out3,
       demultiplexer_1_out4, demultiplexer_1_out5, demultiplexer_1_out6, demultiplexer_1_out7;
  wire [15:0] ram512_1_out16, ram512_2_out16, ram512_3_out16, ram512_4_out16, ram512_5_out16, ram512_6_out16,
       ram512_7_out16, ram512_8_out16;

  Demultiplexer #(.select(3), .enable("false")) demultiplexer_1 (
    .out0(demultiplexer_1_out0), .out1(demultiplexer_1_out1), .out2(demultiplexer_1_out2),
    .out3(demultiplexer_1_out3), .out4(demultiplexer_1_out4), .out5(demultiplexer_1_out5),
    .out6(demultiplexer_1_out6), .out7(demultiplexer_1_out7), .in(load), .sel(address[2:0]));
  RAM512 ram512_1 (.in16(in16), .load(demultiplexer_1_out0), .address(address[11:3]), .out16(ram512_1_out16));
  RAM512 ram512_2 (.in16(in16), .load(demultiplexer_1_out1), .address(address[11:3]), .out16(ram512_2_out16));
  RAM512 ram512_3 (.in16(in16), .load(demultiplexer_1_out2), .address(address[11:3]), .out16(ram512_3_out16));
  RAM512 ram512_4 (.in16(in16), .load(demultiplexer_1_out3), .address(address[11:3]), .out16(ram512_4_out16));
  RAM512 ram512_5 (.in16(in16), .load(demultiplexer_1_out4), .address(address[11:3]), .out16(ram512_5_out16));
  RAM512 ram512_6 (.in16(in16), .load(demultiplexer_1_out5), .address(address[11:3]), .out16(ram512_6_out16));
  RAM512 ram512_7 (.in16(in16), .load(demultiplexer_1_out6), .address(address[11:3]), .out16(ram512_7_out16));
  RAM512 ram512_8 (.in16(in16), .load(demultiplexer_1_out7), .address(address[11:3]), .out16(ram512_8_out16));
  Multiplexer #(.select(3), .width(16), .enable("false")) multiplexer_1 (
    .in0(ram512_1_out16), .in1(ram512_2_out16), .in2(ram512_3_out16), .in3(ram512_4_out16),
    .in4(ram512_5_out16), .in5(ram512_6_out16), .in6(ram512_7_out16), .in7(ram512_8_out16), .out(out16),
    .sel(address[2:0]));

  // Notes on the sheet:
  //   RAM4K
endmodule

module RAM16K (
  input  [15:0] in16,
  input  load,
  input  [13:0] address,
  output [15:0] out16
);

  wire demultiplexer_1_out0, demultiplexer_1_out1, demultiplexer_1_out2, demultiplexer_1_out3;
  wire [15:0] ram4k_1_out16, ram4k_2_out16, ram4k_3_out16, ram4k_4_out16;

  Demultiplexer #(.select(2), .enable("false")) demultiplexer_1 (
    .out0(demultiplexer_1_out0), .out1(demultiplexer_1_out1), .out2(demultiplexer_1_out2),
    .out3(demultiplexer_1_out3), .in(load), .sel(address[1:0]));
  RAM4K ram4k_1 (.in16(in16), .load(demultiplexer_1_out0), .address(address[13:2]), .out16(ram4k_1_out16));
  RAM4K ram4k_2 (.in16(in16), .load(demultiplexer_1_out1), .address(address[13:2]), .out16(ram4k_2_out16));
  RAM4K ram4k_3 (.in16(in16), .load(demultiplexer_1_out2), .address(address[13:2]), .out16(ram4k_3_out16));
  RAM4K ram4k_4 (.in16(in16), .load(demultiplexer_1_out3), .address(address[13:2]), .out16(ram4k_4_out16));
  Multiplexer #(.select(2), .width(16), .enable("false")) multiplexer_1 (
    .in0(ram4k_1_out16), .in1(ram4k_2_out16), .in2(ram4k_3_out16), .in3(ram4k_4_out16), .out(out16),
    .sel(address[1:0]));

  // Notes on the sheet:
  //   RAM16K
endmodule

module PC (
  input  inc,
  input  load,
  input  reset,
  input  [15:0] in16,
  output [15:0] out16
);

  wire clock_1_out;
  wire [15:0] and_1_out, inc16_1_out16, multiplexer_1_out, multiplexer_2_out, multiplexer_3_out, not_1_out;

  Multiplexer #(.width(16), .enable("false")) multiplexer_1 (
    .in0(out16), .in1(inc16_1_out16), .out(multiplexer_1_out), .sel(inc));
  Multiplexer #(.width(16), .enable("false")) multiplexer_2 (
    .in0(multiplexer_1_out), .in1(in16), .out(multiplexer_2_out), .sel(load));
  assign and_1_out = multiplexer_2_out & not_1_out;  // AND_Gate and_1, 16 bits wide
  assign not_1_out = ~multiplexer_2_out;  // NOT_Gate not_1, 16 bits wide
  Register #(.width(16)) register_1 (.D(multiplexer_3_out), .en(1'b1), .clk(clock_1_out), .Q(out16));  // open: clr
  Multiplexer #(.width(16), .enable("false")) multiplexer_3 (
    .in0(multiplexer_2_out), .in1(and_1_out), .out(multiplexer_3_out), .sel(reset));
  Clock clock_1 (.out(clock_1_out));
  Inc16 inc16_1 (.in16(out16), .out16(inc16_1_out16));

  // Notes on the sheet:
  //   Program Counter
endmodule

module CPU (
  input  [15:0] instruction,
  input  [15:0] inM,
  input  reset,
  output writeM,
  output [15:0] outM,
  output [14:0] addressM,
  output [14:0] PC_out
);

  wire alu_1_ng, alu_1_zr, and_2_out, and_3_out, and_4_out, and_5_out, and_6_out, clock_1_out, clock_2_out,
       multiplexer_3_out, not_2_out, not_3_out, not_4_out, not_5_out, not_6_out, or_1_out, or_2_out, or_3_out;
  wire [12:0] and_1_out, multiplexer_1_out, not_1_out;
  wire [15:0] D_register_q, multiplexer_2_out, multiplexer_4_out;
  wire [15:15] A_register_q, pc_1_out16;

  assign not_1_out = ~instruction[12:0];  // NOT_Gate not_1, 13 bits wide
  assign and_1_out = instruction[12:0] & not_1_out;  // AND_Gate and_1, 13 bits wide
  Multiplexer #(.width(13), .enable("false")) multiplexer_1 (
    .in0(and_1_out), .in1(instruction[12:0]),
    .out({multiplexer_1_out[12:4], writeM, multiplexer_1_out[2:0]}), .sel(instruction[15]));
  not not_2 (not_2_out, alu_1_zr);
  not not_3 (not_3_out, alu_1_zr);
  not not_4 (not_4_out, alu_1_ng);
  and and_2 (and_2_out, not_3_out, not_4_out);
  Multiplexer #(.width(16), .enable("false")) multiplexer_2 (
    .in0(instruction), .in1(outM), .out(multiplexer_2_out), .sel(instruction[15]));
  and and_3 (and_3_out, and_2_out, and_2_out);
  and and_4 (and_4_out, alu_1_zr, alu_1_zr);
  and and_5 (and_5_out, alu_1_ng, alu_1_ng);
  and and_6 (and_6_out, not_2_out, not_2_out);
  or or_1 (or_1_out, multiplexer_1_out[5], not_5_out);
  not not_5 (not_5_out, instruction[15]);
  or or_2 (or_2_out, and_3_out, and_4_out);
  or or_3 (or_3_out, and_4_out, and_5_out);
  Register #(.width(16)) A_register (
    .D(multiplexer_2_out), .en(or_1_out), .clk(clock_1_out), .Q({A_register_q[15], addressM}));  // open: clr
  Clock clock_1 (.out(clock_1_out));
  Multiplexer #(.select(3), .enable("false")) multiplexer_3 (
    .in0(1'b0), .in1(and_3_out), .in2(and_4_out), .in3(or_2_out), .in4(and_5_out), .in5(and_6_out),
    .in6(or_3_out), .in7(1'b1), .out(multiplexer_3_out), .sel(multiplexer_1_out[2:0]));
  Register #(.width(16)) D_register (
    .D(outM), .en(multiplexer_1_out[4]), .clk(clock_2_out), .Q(D_register_q));  // open: clr
  Clock clock_2 (.out(clock_2_out));
  Multiplexer #(.width(16), .enable("false")) multiplexer_4 (
    .in0({A_register_q[15], addressM}), .in1(inM), .out(multiplexer_4_out), .sel(multiplexer_1_out[12]));
  not not_6 (not_6_out, multiplexer_3_out);
  ALU alu_1 (
    .zy(multiplexer_1_out[9]), .zx(multiplexer_1_out[11]), .y(multiplexer_4_out), .nx(multiplexer_1_out[10]),
    .f(multiplexer_1_out[7]), .no(multiplexer_1_out[6]), .ng(alu_1_ng), .ny(multiplexer_1_out[8]),
    .x(D_register_q), .zr(alu_1_zr), .out16(outM));
  PC pc_1 (
    .out16({pc_1_out16[15], PC_out}), .in16({A_register_q[15], addressM}), .load(multiplexer_3_out),
    .inc(not_6_out), .reset(reset));

  // Notes on the sheet:
  //   CPU
  //   j1
  //   j2
  //   j3
  //   op
  //   c,d,j
  //   d3=M_reg
  //   d2=D_reg
  //   d1=A_reg
  //   c-instruction
  //   'a' bit
  //   JGT
  //   JEQ
  //   JLT
  //   JNE
  //   ALU output
  //   c6=no
  //   c5=f
  //   JGE
  //   JLE
  //   c4=ny
  //   c3=zy
  //   c2=nx
  //   c1=zx
  //   zr
  //   ng
  //   ALU output
  //   memory address output
endmodule

module Mux8Way (
  input  in_1,
  input  in_2,
  input  in_3,
  input  in_4,
  input  in_5,
  input  in_6,
  input  in_7,
  input  in_8,
  input  [2:0] in_9,
  output out_10
);

  wire multiplexer_1_out, multiplexer_2_out, multiplexer_3_out, multiplexer_4_out, multiplexer_5_out,
       multiplexer_6_out;

  Multiplexer #(.enable("false")) multiplexer_1 (.in0(in_1), .in1(in_2), .out(multiplexer_1_out), .sel(in_9[0]));
  Multiplexer #(.enable("false")) multiplexer_2 (.in0(in_3), .in1(in_4), .out(multiplexer_2_out), .sel(in_9[0]));
  Multiplexer #(.enable("false")) multiplexer_3 (.in0(in_5), .in1(in_6), .out(multiplexer_3_out), .sel(in_9[0]));
  Multiplexer #(.enable("false")) multiplexer_4 (.in0(in_7), .in1(in_8), .out(multiplexer_4_out), .sel(in_9[0]));
  Multiplexer #(.enable("false")) multiplexer_5 (
    .in0(multiplexer_1_out), .in1(multiplexer_2_out), .out(multiplexer_5_out), .sel(in_9[1]));
  Multiplexer #(.enable("false")) multiplexer_6 (
    .in0(multiplexer_3_out), .in1(multiplexer_4_out), .out(multiplexer_6_out), .sel(in_9[1]));
  Multiplexer #(.enable("false")) multiplexer_7 (
    .in0(multiplexer_5_out), .in1(multiplexer_6_out), .out(out_10), .sel(in_9[2]));

  // Notes on the sheet:
  //   Mux8Way
endmodule

module Memory (
  input  [15:0] in16,
  input  [14:0] address15,
  input  load,
  output [15:0] out16
);

  wire and_1_out, clock_1_out, demultiplexer_1_out0, demultiplexer_1_out1;
  wire [15:0] keyboard_q, multiplexer_1_out, ram_1_dout, ram_2_dout;

  and and_1 (and_1_out, address15[13], address15[14]);
  Demultiplexer #(.enable("false")) demultiplexer_1 (
    .out0(demultiplexer_1_out0), .out1(demultiplexer_1_out1), .in(load), .sel(address15[14]));
  Clock clock_1 (.out(clock_1_out));
  RAM #(.addrWidth(14), .dataWidth(16), .databus("bibus")) ram_1 (
    .addr(address15[13:0]), .we(demultiplexer_1_out0), .oe(1'b1), .clk(clock_1_out), .din(in16),
    .dout(ram_1_dout));
  RAM #(.addrWidth(13), .dataWidth(16), .databus("bibus")) ram_2 (
    .addr(address15[12:0]), .we(demultiplexer_1_out1), .oe(1'b1), .clk(clock_1_out), .din(in16),
    .dout(ram_2_dout));
  Register #(.width(16)) keyboard (.clk(clock_1_out), .Q(keyboard_q));  // open: D, en, clr
  Multiplexer #(.width(16), .enable("false")) multiplexer_1 (
    .in0(ram_1_dout), .in1(ram_2_dout), .out(multiplexer_1_out), .sel(address15[14]));
  Multiplexer #(.width(16), .enable("false")) multiplexer_2 (
    .in0(multiplexer_1_out), .in1(keyboard_q), .out(out16), .sel(and_1_out));

  // Notes on the sheet:
  //   Memory
  //   RAM16K + Screen8K + Keyboard
endmodule
